// Logisim project xor_xnor.circ as structural Verilog: 1 circuit, main circuit main
module main (
  input  in_1,
  input  in_2,
  input  in_3,
  input  in_4,
  input  in_5,
  input  in_6,
  input  in_7,
  input  in_8,
  input  in_9,
  input  in_10,
  input  A,
  input  B,
  input  in_13,
  input  in_14,
  output out_15,
  output out_16,
  output out_17,
  output out_18,
  output out_19,
  output out_20,
  output out_21
);

  wire and_1_out, and_2_out, nand_1_out, nand_2_out, nand_3_out, nor_1_out, nor_2_out, nor_3_out, nor_5_out,
       not_1_out, not_2_out, not_3_out, not_4_out, not_5_out, not_6_out, or_1_out, transistor_1_out,
       transistor_3_out;

  not not_1 (not_1_out, in_1);
  not not_2 (not_2_out, in_2);
  not not_3 (not_3_out, in_3);
  not not_4 (not_4_out, in_4);
  or or_1 (or_1_out, in_5, in_6);
  nor nor_1 (nor_1_out, in_8, in_9);
  nand nand_1 (nand_1_out, in_8, in_9);
  and and_1 (and_1_out, not_1_out, in_2);
  nor nor_2 (nor_2_out, not_3_out, in_4);
  nor nor_3 (nor_3_out, not_4_out, in_3);
  nand nand_2 (nand_2_out, in_5, in_6);
  not not_5 (not_5_out, nand_1_out);
  Transistor transistor_1 (.in(1'b1), .out(transistor_1_out), .gate(A));
  Transistor #(.\type ("n")) transistor_2 (.in(1'b0), .out(transistor_1_out), .gate(A));
  Transistor transistor_3 (.in(1'b1), .out(transistor_3_out), .gate(in_13));
  Transistor #(.\type ("n")) transistor_4 (.in(1'b0), .out(transistor_3_out), .gate(in_13));
  and and_2 (and_2_out, in_1, not_2_out);
  and and_3 (out_17, or_1_out, nand_2_out);
  nor nor_4 (out_19, nor_1_out, not_5_out);
  or or_2 (out_15, and_2_out, and_1_out);
  or or_3 (out_16, nor_2_out, nor_3_out);
  Transistor transistor_5 (.in(B), .out(out_20), .gate(transistor_1_out));
  Transistor #(.\type ("n")) transistor_6 (.in(B), .out(out_20), .gate(A));
  Transistor transistor_7 (.in(transistor_3_out), .out(out_21), .gate(in_14));
  Transistor #(.\type ("n")) transistor_8 (.in(in_13), .out(out_21), .gate(in_14));
  Transistor transistor_9 (.in(in_14), .out(out_21), .gate(transistor_3_out));
  Transistor #(.\type ("n")) transistor_10 (.in(in_14), .out(out_21), .gate(in_13));
  Transistor transistor_11 (.in(transistor_1_out), .out(out_20), .gate(B));
  Transistor #(.\type ("n")) transistor_12 (.in(A), .out(out_20), .gate(B));
  nand nand_3 (nand_3_out, in_7, in_10);
  not not_6 (not_6_out, nand_3_out);
  nor nor_5 (nor_5_out, in_7, in_10);
  or or_4 (out_18, not_6_out, nor_5_out);

  // Notes on the sheet:
  //   异或（1）：22
  //   异或（2）：18
  //   异或（3）：16
  //   异或（4）：14
  //   晶体管层次同或门
  //   同或门
endmodule
