// Logisim project sCPU.circ as structural Verilog
module ROM_array (
  input  WE,
  output [7:0] out_2
);

  wire clock_1_out;
  wire [7:0] adder_1_out, PC_q;

  Clock clock_1 (.out(clock_1_out));
  Adder adder_1 (.a(8'h1), .b(PC_q), .out(adder_1_out));  // open: cin, cout
  Register PC (.D(adder_1_out), .en(WE), .clk(clock_1_out), .Q(PC_q));  // open: clr
  Multiplexer #(.select(3), .width(8)) multiplexer_1 (
    .in0(8'h8a), .in1(8'h90), .in2(8'ha0), .in3(8'hb1), .in4(8'h17), .in5(8'h29), .in6(8'hd1), .in7(8'hdf),
    .out(out_2), .sel(PC_q[2:0]));
  // Probe on 8'h90
  // Probe on 8'h8a
endmodule

module gpr (
  input  [7:0] wr,
  input  we,
  input  [1:0] addr,
  input  [1:0] in_4,
  output [7:0] re
);

  wire clock_1_out, decoder_1_out0, decoder_1_out1, decoder_1_out2, decoder_1_out3;
  wire [7:0] r0_q, r1_q, r2_q, r3_q;

  Decoder #(.select(2)) decoder_1 (
    .out0(decoder_1_out0), .out1(decoder_1_out1), .out2(decoder_1_out2), .out3(decoder_1_out3), .sel(addr),
    .en(we));
  Clock clock_1 (.out(clock_1_out));
  Register r0 (.D(wr), .en(decoder_1_out0), .clk(clock_1_out), .Q(r0_q));  // open: clr
  Register r2 (.D(wr), .en(decoder_1_out2), .clk(clock_1_out), .Q(r2_q));  // open: clr
  Register r1 (.D(wr), .en(decoder_1_out1), .clk(clock_1_out), .Q(r1_q));  // open: clr
  Register r3 (.D(wr), .en(decoder_1_out3), .clk(clock_1_out), .Q(r3_q));  // open: clr
  Multiplexer #(.select(2), .width(8)) multiplexer_1 (
    .in0(r0_q), .in1(r1_q), .in2(r2_q), .in3(r3_q), .out(re), .sel(in_4));
endmodule

module scpu_li (
  input  in_1,
  input  [1:0] in_2,
  output [7:0] out_3
);

  wire and_1_out, not_1_out;
  wire [7:0] rom_array_1_out_2;

  ROM_array rom_array_1 (.WE(in_1), .out_2(rom_array_1_out_2));
  and and_1 (and_1_out, rom_array_1_out_2[7], not_1_out);
  not not_1 (not_1_out, rom_array_1_out_2[6]);
  gpr gpr_1 (
    .wr({4'b0000, rom_array_1_out_2[3:0]}), .we(and_1_out), .addr(rom_array_1_out_2[5:4]), .in_4(in_2),
    .re(out_3));
endmodule

module scpu_add (
  input  in_1
);

  wire and_1_out, clock_1_out, decoder_1_out0, decoder_1_out1, decoder_1_out2, decoder_1_out3, nor_1_out,
       not_1_out, or_1_out;
  wire [7:0] adder_1_out, multiplexer_1_out, multiplexer_2_out, multiplexer_3_out, r0_q, r1_q, r2_q, r3_q,
       rom_array_1_out_2;

  Clock clock_1 (.out(clock_1_out));
  ROM_array rom_array_1 (.WE(in_1), .out_2(rom_array_1_out_2));
  nor nor_1 (nor_1_out, rom_array_1_out_2[7], rom_array_1_out_2[6]);
  or or_1 (or_1_out, nor_1_out, and_1_out);
  not not_1 (not_1_out, rom_array_1_out_2[6]);
  and and_1 (and_1_out, rom_array_1_out_2[7], not_1_out);
  Multiplexer #(.width(8)) multiplexer_1 (
    .in0(adder_1_out), .in1({4'b0000, rom_array_1_out_2[3:0]}), .out(multiplexer_1_out), .sel(and_1_out));
  Decoder #(.select(2)) decoder_1 (
    .out0(decoder_1_out0), .out1(decoder_1_out1), .out2(decoder_1_out2), .out3(decoder_1_out3),
    .sel(rom_array_1_out_2[5:4]), .en(or_1_out));
  Register r0 (.D(multiplexer_1_out), .en(decoder_1_out0), .clk(clock_1_out), .Q(r0_q));  // open: clr
  Register r2 (.D(multiplexer_1_out), .en(decoder_1_out2), .clk(clock_1_out), .Q(r2_q));  // open: clr
  // Probe on r0_q
  // Probe on r1_q
  // Probe on r2_q
  // Probe on r3_q
  Register r1 (.D(multiplexer_1_out), .en(decoder_1_out1), .clk(clock_1_out), .Q(r1_q));  // open: clr
  Register r3 (.D(multiplexer_1_out), .en(decoder_1_out3), .clk(clock_1_out), .Q(r3_q));  // open: clr
  Multiplexer #(.select(2), .width(8)) multiplexer_2 (
    .in0(r0_q), .in1(r1_q), .in2(r2_q), .in3(r3_q), .out(multiplexer_2_out), .sel(rom_array_1_out_2[1:0]));
  Multiplexer #(.select(2), .width(8)) multiplexer_3 (
    .in0(r0_q), .in1(r1_q), .in2(r2_q), .in3(r3_q), .out(multiplexer_3_out), .sel(rom_array_1_out_2[3:2]));
  Adder adder_1 (.a(multiplexer_2_out), .b(multiplexer_3_out), .out(adder_1_out));  // open: cin, cout
endmodule

module scpu_bner0 (
  input  WE
);

  wire and_1_out, and_2_out, and_3_out, clock_1_out, comparator_1_eq, decoder_1_out0, decoder_1_out1,
       decoder_1_out2, decoder_1_out3, nor_1_out, not_1_out, not_2_out, or_1_out;
  wire [1:0] multiplexer_2_out_2;
  wire [3:0] multiplexer_2_out_3;
  wire [7:0] adder_1_out, adder_2_out, multiplexer_1_out, multiplexer_3_out, multiplexer_4_out,
       multiplexer_5_out, multiplexer_6_out, PC_q, r0_q, r1_q, r2_q, r3_q;
  wire [7:6] multiplexer_2_out;

  Clock clock_1 (.out(clock_1_out));
  // Probe on {4'b0000, multiplexer_2_out_2, multiplexer_2_out_3[3:2]}
  Adder adder_1 (.a(8'h1), .b(PC_q), .out(adder_1_out));  // open: cin, cout
  // Probe on and_1_out
  // Probe on multiplexer_1_out
  Multiplexer #(.width(8)) multiplexer_1 (
    .in0(adder_1_out), .in1({4'b0000, multiplexer_2_out_2, multiplexer_2_out_3[3:2]}),
    .out(multiplexer_1_out), .sel(and_1_out));
  Register PC (.D(multiplexer_1_out), .en(WE), .clk(clock_1_out), .Q(PC_q));  // open: clr
  Multiplexer #(.select(3), .width(8)) multiplexer_2 (
    .in0(8'h8a), .in1(8'h90), .in2(8'ha0), .in3(8'hb1), .in4(8'h17), .in5(8'h29), .in6(8'hd1), .in7(8'hdf),
    .out({multiplexer_2_out, multiplexer_2_out_2, multiplexer_2_out_3}), .sel(PC_q[2:0]));
  // Probe on 8'h90
  // Probe on 8'h8a
  and and_1 (and_1_out, and_2_out, not_1_out);
  and and_2 (and_2_out, multiplexer_2_out[7], multiplexer_2_out[6]);
  and and_3 (and_3_out, multiplexer_2_out[7], not_2_out);
  nor nor_1 (nor_1_out, multiplexer_2_out[7], multiplexer_2_out[6]);
  or or_1 (or_1_out, nor_1_out, and_3_out);
  not not_1 (not_1_out, comparator_1_eq);
  not not_2 (not_2_out, multiplexer_2_out[6]);
  Multiplexer #(.width(8)) multiplexer_3 (
    .in0(adder_2_out), .in1({4'b0000, multiplexer_2_out_3}), .out(multiplexer_3_out), .sel(and_3_out));
  Decoder #(.select(2)) decoder_1 (
    .out0(decoder_1_out0), .out1(decoder_1_out1), .out2(decoder_1_out2), .out3(decoder_1_out3),
    .sel(multiplexer_2_out_2), .en(or_1_out));
  Register r0 (.D(multiplexer_3_out), .en(decoder_1_out0), .clk(clock_1_out), .Q(r0_q));  // open: clr
  Register r2 (.D(multiplexer_3_out), .en(decoder_1_out2), .clk(clock_1_out), .Q(r2_q));  // open: clr
  // Probe on r0_q
  // Probe on r1_q
  // Probe on r2_q
  // Probe on r3_q
  Register r1 (.D(multiplexer_3_out), .en(decoder_1_out1), .clk(clock_1_out), .Q(r1_q));  // open: clr
  Register r3 (.D(multiplexer_3_out), .en(decoder_1_out3), .clk(clock_1_out), .Q(r3_q));  // open: clr
  Multiplexer #(.select(2), .width(8)) multiplexer_4 (
    .in0(r0_q), .in1(r1_q), .in2(r2_q), .in3(r3_q), .out(multiplexer_4_out), .sel(multiplexer_2_out_3[1:0]));
  Multiplexer #(.select(2), .width(8)) multiplexer_5 (
    .in0(r0_q), .in1(r1_q), .in2(r2_q), .in3(r3_q), .out(multiplexer_5_out), .sel(multiplexer_2_out_3[3:2]));
  Multiplexer #(.width(8)) multiplexer_6 (
    .in0(multiplexer_5_out), .in1(r0_q), .out(multiplexer_6_out), .sel(and_2_out));
  Adder adder_2 (.a(multiplexer_4_out), .b(multiplexer_5_out), .out(adder_2_out));  // open: cin, cout
  Comparator comparator_1 (.a(multiplexer_4_out), .b(multiplexer_6_out), .eq(comparator_1_eq));  // open: gt, lt
endmodule

module scpu_oddsum (
  input  WE
);

  wire and_1_out, and_2_out, and_3_out, clock_1_out, comparator_1_eq, decoder_1_out0, decoder_1_out1,
       decoder_1_out2, decoder_1_out3, nor_1_out, not_1_out, not_2_out, or_1_out;
  wire [2:0] PC_q_2;
  wire [7:0] adder_1_out, adder_2_out, multiplexer_1_out, multiplexer_2_out, multiplexer_3_out,
       multiplexer_4_out, multiplexer_5_out, multiplexer_6_out, r0_q, r1_q, r2_q, r3_q;
  wire [7:3] PC_q;

  Clock clock_1 (.out(clock_1_out));
  // Probe on {4'b0000, multiplexer_2_out[5:2]}
  // Probe on and_2_out
  Adder adder_1 (.a(8'h1), .b({PC_q, PC_q_2}), .out(adder_1_out));  // open: cin, cout
  // Probe on multiplexer_1_out
  Multiplexer #(.width(8)) multiplexer_1 (
    .in0(adder_1_out), .in1({4'b0000, multiplexer_2_out[5:2]}), .out(multiplexer_1_out), .sel(and_2_out));
  Register PC (.D(multiplexer_1_out), .en(WE), .clk(clock_1_out), .Q({PC_q, PC_q_2}));  // open: clr
  Multiplexer #(.select(3), .width(8)) multiplexer_2 (
    .in0(8'h89), .in1(8'h91), .in2(8'ha1), .in3(8'hb2), .in4(8'h17), .in5(8'h29), .in6(8'hd1), .in7(8'hdf),
    .out(multiplexer_2_out), .sel(PC_q_2));
  // Probe on 8'h91
  // Probe on 8'h89
  and and_1 (and_1_out, multiplexer_2_out[7], multiplexer_2_out[6]);
  and and_2 (and_2_out, and_1_out, not_1_out);
  nor nor_1 (nor_1_out, multiplexer_2_out[7], multiplexer_2_out[6]);
  or or_1 (or_1_out, nor_1_out, and_3_out);
  not not_1 (not_1_out, comparator_1_eq);
  not not_2 (not_2_out, multiplexer_2_out[6]);
  and and_3 (and_3_out, multiplexer_2_out[7], not_2_out);
  Multiplexer #(.width(8)) multiplexer_3 (
    .in0(adder_2_out), .in1({4'b0000, multiplexer_2_out[3:0]}), .out(multiplexer_3_out), .sel(and_3_out));
  Decoder #(.select(2)) decoder_1 (
    .out0(decoder_1_out0), .out1(decoder_1_out1), .out2(decoder_1_out2), .out3(decoder_1_out3),
    .sel(multiplexer_2_out[5:4]), .en(or_1_out));
  Register r0 (.D(multiplexer_3_out), .en(decoder_1_out0), .clk(clock_1_out), .Q(r0_q));  // open: clr
  Register r2 (.D(multiplexer_3_out), .en(decoder_1_out2), .clk(clock_1_out), .Q(r2_q));  // open: clr
  // Probe on r0_q
  // Probe on r1_q
  // Probe on r2_q
  // Probe on r3_q
  Register r1 (.D(multiplexer_3_out), .en(decoder_1_out1), .clk(clock_1_out), .Q(r1_q));  // open: clr
  Register r3 (.D(multiplexer_3_out), .en(decoder_1_out3), .clk(clock_1_out), .Q(r3_q));  // open: clr
  Multiplexer #(.select(2), .width(8)) multiplexer_4 (
    .in0(r0_q), .in1(r1_q), .in2(r2_q), .in3(r3_q), .out(multiplexer_4_out), .sel(multiplexer_2_out[1:0]));
  Multiplexer #(.select(2), .width(8)) multiplexer_5 (
    .in0(r0_q), .in1(r1_q), .in2(r2_q), .in3(r3_q), .out(multiplexer_5_out), .sel(multiplexer_2_out[3:2]));
  Multiplexer #(.width(8)) multiplexer_6 (
    .in0(multiplexer_5_out), .in1(r0_q), .out(multiplexer_6_out), .sel(and_1_out));
  Adder adder_2 (.a(multiplexer_4_out), .b(multiplexer_5_out), .out(adder_2_out));  // open: cin, cout
  Comparator comparator_1 (.a(multiplexer_4_out), .b(multiplexer_6_out), .eq(comparator_1_eq));  // open: gt, lt
endmodule
