// Logisim project sCPU.circ as structural Verilog
module ROM_array (
  input  WE,
  output [7:0] out_2
);

  wire clock_1_out;
  wire [7:0] adder_1_out, PC_q;

  Clock clock_1 (.out(clock_1_out));
  Adder adder_1 (.a(8'h1), .b(PC_q), .out(adder_1_out));  // open: cin, cout
  Register PC (.D(adder_1_out), .en(WE), .clk(clock_1_out), .Q(PC_q));  // open: clr
  Multiplexer #(.select(3), .width(8)) multiplexer_1 (
    .in0(8'h8a), .in1(8'h90), .in2(8'ha0), .in3(8'hb1), .in4(8'h17), .in5(8'h29), .in6(8'hd1), .in7(8'hdf),
    .out(out_2), .sel(PC_q[2:0]));
  // Probe on 8'h90
  // Probe on 8'h8a
endmodule

module gpr (
  input  [7:0] wr,
  input  we,
  input  [1:0] addr,
  input  [1:0] in_4,
  output [7:0] re
);

  wire clock_1_out, decoder_1_out0, decoder_1_out1, decoder_1_out2, decoder_1_out3;
  wire [7:0] r0_q, r1_q, r2_q, r3_q;

  Decoder #(.select(2)) decoder_1 (
    .out0(decoder_1_out0), .out1(decoder_1_out1), .out2(decoder_1_out2), .out3(decoder_1_out3), .sel(addr),
    .en(we));
  Clock clock_1 (.out(clock_1_out));
  Register r0 (.D(wr), .en(decoder_1_out0), .clk(clock_1_out), .Q(r0_q));  // open: clr
  Register r2 (.D(wr), .en(decoder_1_out2), .clk(clock_1_out), .Q(r2_q));  // open: clr
  Register r1 (.D(wr), .en(decoder_1_out1), .clk(clock_1_out), .Q(r1_q));  // open: clr
  Register r3 (.D(wr), .en(decoder_1_out3), .clk(clock_1_out), .Q(r3_q));  // open: clr
  Multiplexer #(.select(2), .width(8)) multiplexer_1 (
    .in0(r0_q), .in1(r1_q), .in2(r2_q), .in3(r3_q), .out(re), .sel(in_4));
endmodule

module scpu_li (
  input  in_1,
  input  [1:0] in_2,
  output [7:0] out_3
);

  wire and_1_out, not_1_out;
  wire [7:0] rom_array_1_out_2;

  ROM_array rom_array_1 (.WE(in_1), .out_2(rom_array_1_out_2));
  and and_1 (and_1_out, rom_array_1_out_2[7], not_1_out);
  not not_1 (not_1_out, rom_array_1_out_2[6]);
  gpr gpr_1 (
    .wr({4'b0000, rom_array_1_out_2[3:0]}), .we(and_1_out), .addr(rom_array_1_out_2[5:4]), .in_4(in_2),
    .re(out_3));
endmodule

module scpu_add (
  input  in_1
);

  wire and_1_out, clock_1_out, decoder_1_out0, decoder_1_out1, decoder_1_out2, decoder_1_out3, nor_1_out,
       not_1_out, or_1_out;
  wire [7:0] adder_1_out, multiplexer_1_out, multiplexer_2_out, multiplexer_3_out, r0_q, r1_q, r2_q, r3_q,
       rom_array_1_out_2;

  Clock clock_1 (.out(clock_1_out));
  ROM_array rom_array_1 (.WE(in_1), .out_2(rom_array_1_out_2));
  nor nor_1 (nor_1_out, rom_array_1_out_2[7], rom_array_1_out_2[6]);
  or or_1 (or_1_out, nor_1_out, and_1_out);
  not not_1 (not_1_out, rom_array_1_out_2[6]);
  and and_1 (and_1_out, rom_array_1_out_2[7], not_1_out);
  Multiplexer #(.width(8)) multiplexer_1 (
    .in0(adder_1_out), .in1({4'b0000, rom_array_1_out_2[3:0]}), .out(multiplexer_1_out), .sel(and_1_out));
  Decoder #(.select(2)) decoder_1 (
    .out0(decoder_1_out0), .out1(decoder_1_out1), .out2(decoder_1_out2), .out3(decoder_1_out3),
    .sel(rom_array_1_out_2[5:4]), .en(or_1_out));
  Register r0 (.D(multiplexer_1_out), .en(decoder_1_out0), .clk(clock_1_out), .Q(r0_q));  // open: clr
  Register r2 (.D(multiplexer_1_out), .en(decoder_1_out2), .clk(clock_1_out), .Q(r2_q));  // open: clr
  // Probe on r0_q
  // Probe on r1_q
  // Probe on r2_q
  // Probe on r3_q
  Register r1 (.D(multiplexer_1_out), .en(decoder_1_out1), .clk(clock_1_out), .Q(r1_q));  // open: clr
  Register r3 (.D(multiplexer_1_out), .en(decoder_1_out3), .clk(clock_1_out), .Q(r3_q));  // open: clr
  Multiplexer #(.select(2), .width(8)) multiplexer_2 (
    .in0(r0_q), .in1(r1_q), .in2(r2_q), .in3(r3_q), .out(multiplexer_2_out), .sel(rom_array_1_out_2[1:0]));
  Multiplexer #(.select(2), .width(8)) multiplexer_3 (
    .in0(r0_q), .in1(r1_q), .in2(r2_q), .in3(r3_q), .out(multiplexer_3_out), .sel(rom_array_1_out_2[3:2]));
  Adder adder_1 (.a(multiplexer_2_out), .b(multiplexer_3_out), .out(adder_1_out));  // open: cin, cout
endmodule

module scpu_bner0 (
  input  WE
);

  wire and_1_out, and_2_out, and_3_out, clock_1_out, comparator_1_eq, decoder_1_out0, decoder_1_out1,
       decoder_1_out2, decoder_1_out3, nor_1_out, not_1_out, not_2_out, or_1_out;
  wire [1:0] multiplexer_2_out_2;
  wire [3:0] multiplexer_2_out_3;
  wire [7:0] adder_1_out, adder_2_out, multiplexer_1_out, multiplexer_3_out, multiplexer_4_out,
       multiplexer_5_out, multiplexer_6_out, PC_q, r0_q, r1_q, r2_q, r3_q;
  wire [7:6] multiplexer_2_out;

  Clock clock_1 (.out(clock_1_out));
  // Probe on {4'b0000, multiplexer_2_out_2, multiplexer_2_out_3[3:2]}
  Adder adder_1 (.a(8'h1), .b(PC_q), .out(adder_1_out));  // open: cin, cout
  // Probe on and_1_out
  // Probe on multiplexer_1_out
  Multiplexer #(.width(8)) multiplexer_1 (
    .in0(adder_1_out), .in1({4'b0000, multiplexer_2_out_2, multiplexer_2_out_3[3:2]}),
    .out(multiplexer_1_out), .sel(and_1_out));
  Register PC (.D(multiplexer_1_out), .en(WE), .clk(clock_1_out), .Q(PC_q));  // open: clr
  Multiplexer #(.select(3), .width(8)) multiplexer_2 (
    .in0(8'h8a), .in1(8'h90), .in2(8'ha0), .in3(8'hb1), .in4(8'h17), .in5(8'h29), .in6(8'hd1), .in7(8'hdf),
    .out({multiplexer_2_out, multiplexer_2_out_2, multiplexer_2_out_3}), .sel(PC_q[2:0]));
  // Probe on 8'h90
  // Probe on 8'h8a
  and and_1 (and_1_out, and_2_out, not_1_out);
  and and_2 (and_2_out, multiplexer_2_out[7], multiplexer_2_out[6]);
  and and_3 (and_3_out, multiplexer_2_out[7], not_2_out);
  nor nor_1 (nor_1_out, multiplexer_2_out[7], multiplexer_2_out[6]);
  or or_1 (or_1_out, nor_1_out, and_3_out);
  not not_1 (not_1_out, comparator_1_eq);
  not not_2 (not_2_out, multiplexer_2_out[6]);
  Multiplexer #(.width(8)) multiplexer_3 (
    .in0(adder_2_out), .in1({4'b0000, multiplexer_2_out_3}), .out(multiplexer_3_out), .sel(and_3_out));
  Decoder #(.select(2)) decoder_1 (
    .out0(decoder_1_out0), .out1(decoder_1_out1), .out2(decoder_1_out2), .out3(decoder_1_out3),
    .sel(multiplexer_2_out_2), .en(or_1_out));
  Register r0 (.D(multiplexer_3_out), .en(decoder_1_out0), .clk(clock_1_out), .Q(r0_q));  // open: clr
  Register r2 (.D(multiplexer_3_out), .en(decoder_1_out2), .clk(clock_1_out), .Q(r2_q));  // open: clr
  // Probe on r0_q
  // Probe on r1_q
  // Probe on r2_q
  // Probe on r3_q
  Register r1 (.D(multiplexer_3_out), .en(decoder_1_out1), .clk(clock_1_out), .Q(r1_q));  // open: clr
  Register r3 (.D(multiplexer_3_out), .en(decoder_1_out3), .clk(clock_1_out), .Q(r3_q));  // open: clr
  Multiplexer #(.select(2), .width(8)) multiplexer_4 (
    .in0(r0_q), .in1(r1_q), .in2(r2_q), .in3(r3_q), .out(multiplexer_4_out), .sel(multiplexer_2_out_3[1:0]));
  Multiplexer #(.select(2), .width(8)) multiplexer_5 (
    .in0(r0_q), .in1(r1_q), .in2(r2_q), .in3(r3_q), .out(multiplexer_5_out), .sel(multiplexer_2_out_3[3:2]));
  Multiplexer #(.width(8)) multiplexer_6 (
    .in0(multiplexer_5_out), .in1(r0_q), .out(multiplexer_6_out), .sel(and_2_out));
  Adder adder_2 (.a(multiplexer_4_out), .b(multiplexer_5_out), .out(adder_2_out));  // open: cin, cout
  Comparator comparator_1 (.a(multiplexer_4_out), .b(multiplexer_6_out), .eq(comparator_1_eq));  // open: gt, lt
endmodule

module scpu_oddsum (
  input  WE
);

  wire and_1_out, and_2_out, and_3_out, clock_1_out, comparator_1_eq, decoder_1_out0, decoder_1_out1,
       decoder_1_out2, decoder_1_out3, nor_1_out, not_1_out, not_2_out, or_1_out;
  wire [2:0] PC_q_2;
  wire [7:0] adder_1_out, adder_2_out, multiplexer_1_out, multiplexer_2_out, multiplexer_3_out,
       multiplexer_4_out, multiplexer_5_out, multiplexer_6_out, r0_q, r1_q, r2_q, r3_q;
  wire [7:3] PC_q;

  Clock clock_1 (.out(clock_1_out));
  // Probe on {4'b0000, multiplexer_2_out[5:2]}
  // Probe on and_2_out
  Adder adder_1 (.a(8'h1), .b({PC_q, PC_q_2}), .out(adder_1_out));  // open: cin, cout
  // Probe on multiplexer_1_out
  Multiplexer #(.width(8)) multiplexer_1 (
    .in0(adder_1_out), .in1({4'b0000, multiplexer_2_out[5:2]}), .out(multiplexer_1_out), .sel(and_2_out));
  Register PC (.D(multiplexer_1_out), .en(WE), .clk(clock_1_out), .Q({PC_q, PC_q_2}));  // open: clr
  Multiplexer #(.select(3), .width(8)) multiplexer_2 (
    .in0(8'h89), .in1(8'h91), .in2(8'ha1), .in3(8'hb2), .in4(8'h17), .in5(8'h29), .in6(8'hd1), .in7(8'hdf),
    .out(multiplexer_2_out), .sel(PC_q_2));
  // Probe on 8'h91
  // Probe on 8'h89
  and and_1 (and_1_out, multiplexer_2_out[7], multiplexer_2_out[6]);
  and and_2 (and_2_out, and_1_out, not_1_out);
  nor nor_1 (nor_1_out, multiplexer_2_out[7], multiplexer_2_out[6]);
  or or_1 (or_1_out, nor_1_out, and_3_out);
  not not_1 (not_1_out, comparator_1_eq);
  not not_2 (not_2_out, multiplexer_2_out[6]);
  and and_3 (and_3_out, multiplexer_2_out[7], not_2_out);
  Multiplexer #(.width(8)) multiplexer_3 (
    .in0(adder_2_out), .in1({4'b0000, multiplexer_2_out[3:0]}), .out(multiplexer_3_out), .sel(and_3_out));
  Decoder #(.select(2)) decoder_1 (
    .out0(decoder_1_out0), .out1(decoder_1_out1), .out2(decoder_1_out2), .out3(decoder_1_out3),
    .sel(multiplexer_2_out[5:4]), .en(or_1_out));
  Register r0 (.D(multiplexer_3_out), .en(decoder_1_out0), .clk(clock_1_out), .Q(r0_q));  // open: clr
  Register r2 (.D(multiplexer_3_out), .en(decoder_1_out2), .clk(clock_1_out), .Q(r2_q));  // open: clr
  // Probe on r0_q
  // Probe on r1_q
  // Probe on r2_q
  // Probe on r3_q
  Register r1 (.D(multiplexer_3_out), .en(decoder_1_out1), .clk(clock_1_out), .Q(r1_q));  // open: clr
  Register r3 (.D(multiplexer_3_out), .en(decoder_1_out3), .clk(clock_1_out), .Q(r3_q));  // open: clr
  Multiplexer #(.select(2), .width(8)) multiplexer_4 (
    .in0(r0_q), .in1(r1_q), .in2(r2_q), .in3(r3_q), .out(multiplexer_4_out), .sel(multiplexer_2_out[1:0]));
  Multiplexer #(.select(2), .width(8)) multiplexer_5 (
    .in0(r0_q), .in1(r1_q), .in2(r2_q), .in3(r3_q), .out(multiplexer_5_out), .sel(multiplexer_2_out[3:2]));
  Multiplexer #(.width(8)) multiplexer_6 (
    .in0(multiplexer_5_out), .in1(r0_q), .out(multiplexer_6_out), .sel(and_1_out));
  Adder adder_2 (.a(multiplexer_4_out), .b(multiplexer_5_out), .out(adder_2_out));  // open: cin, cout
  Comparator comparator_1 (.a(multiplexer_4_out), .b(multiplexer_6_out), .eq(comparator_1_eq));  // open: gt, lt
endmodule

module scpu_enhance (
  input  WE
);

  wire and_1_out, and_2_out, and_3_out, and_4_out, and_5_out, and_6_out, and_7_out, and_8_out, clock_1_out,
       comparator_1_eq, decoder_1_out0, decoder_1_out1, decoder_1_out2, decoder_1_out3, decoder_2_out0,
       decoder_2_out1, nor_1_out, not_1_out, not_2_out, not_3_out, not_4_out, or_1_out;
  wire [1:0] multiplexer_6_out;
  wire [3:0] register_1_q, register_1_q_2;
  wire [7:0] adder_1_out, adder_2_out, button_8_out, dipswitch_1_p1, multiplexer_1_out, multiplexer_2_out,
       multiplexer_3_out, multiplexer_4_out, multiplexer_5_out, multiplexer_7_out, multiplexer_8_out,
       multiplexer_9_out, multiplexer_10_out, PC_q, r0_q, r1_q, r2_q, r3_q, register_2_q, undriven;

  // Probe on {{5{multiplexer_2_out[5]}}, multiplexer_2_out[4:2]}
  Clock clock_1 (.out(clock_1_out));
  Multiplexer #(.width(8)) multiplexer_1 (
    .in0(8'h1), .in1({{5{multiplexer_2_out[5]}}, multiplexer_2_out[4:2]}), .out(multiplexer_1_out),
    .sel(and_2_out));
  // Probe on and_2_out
  Adder adder_1 (.a(multiplexer_1_out), .b(PC_q), .out(adder_1_out));  // open: cin, cout
  // Probe on adder_1_out
  Register PC (.D(adder_1_out), .en(WE), .clk(clock_1_out), .Q(PC_q));  // open: clr
  Multiplexer #(.select(4), .width(8)) multiplexer_2 (
    .in0(8'h90), .in1(8'ha0), .in2(8'hb1), .in3(8'h17), .in4(8'h26), .in5(8'h58), .in6(8'h69), .in7(8'h41),
    .in8({8{1'b1}}), .in9(8'h40), .in10(8'he5), .in11(8'hc2), .in12(undriven), .in13(8'hc2),
    .out(multiplexer_2_out), .sel(PC_q[3:0]));  // open: in14, in15
  and and_1 (and_1_out, multiplexer_2_out[7], multiplexer_2_out[6]);
  and and_2 (and_2_out, and_1_out, not_1_out);
  nor nor_1 (nor_1_out, multiplexer_2_out[7], multiplexer_2_out[6]);
  or or_1 (or_1_out, nor_1_out, and_5_out, and_3_out);
  not not_1 (not_1_out, comparator_1_eq);
  not not_2 (not_2_out, multiplexer_2_out[6]);
  not not_3 (not_3_out, multiplexer_2_out[7]);
  and and_3 (and_3_out, multiplexer_2_out[7], not_2_out);
  not not_4 (not_4_out, multiplexer_2_out[3]);
  and and_4 (and_4_out, not_3_out, multiplexer_2_out[6]);
  and and_5 (and_5_out, and_4_out, not_4_out);
  Multiplexer #(.select(2), .width(8)) multiplexer_3 (
    .in0({{6{1'b0}}, multiplexer_2_out[1:0]}), .in1({4'b0000, multiplexer_2_out[1:0], 2'b00}),
    .in2({2'b00, multiplexer_2_out[1:0], 4'b0000}), .in3({multiplexer_2_out[1:0], {6{1'b0}}}),
    .out(multiplexer_3_out), .sel(multiplexer_2_out[3:2]));
  Multiplexer #(.width(8)) multiplexer_4 (
    .in0(adder_2_out), .in1(multiplexer_3_out), .out(multiplexer_4_out), .sel(and_3_out));
  Decoder #(.select(2)) decoder_1 (
    .out0(decoder_1_out0), .out1(decoder_1_out1), .out2(decoder_1_out2), .out3(decoder_1_out3),
    .sel(multiplexer_2_out[5:4]), .en(or_1_out));
  Decoder #(.select(3)) decoder_2 (
    .out0(decoder_2_out0), .out1(decoder_2_out1), .sel(multiplexer_2_out[2:0]), .en(and_4_out));  // open: out2, out3, out4, out5, out6, out7
  Multiplexer #(.width(8)) multiplexer_5 (
    .in0(multiplexer_4_out), .in1(multiplexer_10_out), .out(multiplexer_5_out), .sel(and_5_out));
  and and_6 (and_6_out, multiplexer_2_out[3], and_4_out);
  Register r0 (.D(multiplexer_5_out), .en(decoder_1_out0), .clk(clock_1_out), .Q(r0_q));  // open: clr
  Register r2 (.D(multiplexer_5_out), .en(decoder_1_out2), .clk(clock_1_out), .Q(r2_q));  // open: clr
  // Probe on r0_q
  Register r1 (.D(multiplexer_5_out), .en(decoder_1_out1), .clk(clock_1_out), .Q(r1_q));  // open: clr
  Register r3 (.D(multiplexer_5_out), .en(decoder_1_out3), .clk(clock_1_out), .Q(r3_q));  // open: clr
  Multiplexer #(.width(2)) multiplexer_6 (
    .in0(multiplexer_2_out[1:0]), .in1(multiplexer_2_out[5:4]), .out(multiplexer_6_out), .sel(and_6_out));
  Multiplexer #(.select(2), .width(8)) multiplexer_7 (
    .in0(r0_q), .in1(r1_q), .in2(r2_q), .in3(r3_q), .out(multiplexer_7_out), .sel(multiplexer_6_out));
  Multiplexer #(.select(2), .width(8)) multiplexer_8 (
    .in0(r0_q), .in1(r1_q), .in2(r2_q), .in3(r3_q), .out(multiplexer_8_out), .sel(multiplexer_2_out[3:2]));
  Register register_1 (
    .D(multiplexer_7_out), .en(and_7_out), .clk(clock_1_out), .Q({register_1_q_2, register_1_q}));  // open: clr
  and and_7 (and_7_out, decoder_2_out1, and_6_out);
  Register register_2 (.D(multiplexer_7_out), .en(and_8_out), .clk(clock_1_out), .Q(register_2_q));  // open: clr
  and and_8 (and_8_out, decoder_2_out0, and_6_out);
  Button button_1 (.out(button_8_out[7]));
  Multiplexer #(.width(8)) multiplexer_9 (
    .in0(multiplexer_8_out), .in1(r0_q), .out(multiplexer_9_out), .sel(and_1_out));
  // DipSwitch dipswitch_1: pin names not known; wires that end beside it: dipswitch_1_p1[0], dipswitch_1_p1[1], dipswitch_1_p1[2], dipswitch_1_p1[3], dipswitch_1_p1[4], dipswitch_1_p1[5], dipswitch_1_p1[6], dipswitch_1_p1[7]
  Button button_2 (.out(button_8_out[6]));
  Button button_3 (.out(button_8_out[5]));
  Adder adder_2 (.a(multiplexer_7_out), .b(multiplexer_8_out), .out(adder_2_out));  // open: cin, cout
  Comparator comparator_1 (.a(multiplexer_7_out), .b(multiplexer_9_out), .eq(comparator_1_eq));  // open: gt, lt
  Hex_Digit_Display #(.decimalPoint("false")) hex_digit_display_1 (.value(register_1_q_2));
  Hex_Digit_Display #(.decimalPoint("false")) hex_digit_display_2 (.value(register_1_q));
  LedBar ledbar_1 (
    .led0(register_2_q[7]), .led1(register_2_q[6]), .led2(register_2_q[5]), .led3(register_2_q[4]),
    .led4(register_2_q[3]), .led5(register_2_q[2]), .led6(register_2_q[1]), .led7(register_2_q[0]));
  Button button_4 (.out(button_8_out[4]));
  Button button_5 (.out(button_8_out[3]));
  Button button_6 (.out(button_8_out[2]));
  Button button_7 (.out(button_8_out[1]));
  Button button_8 (.out(button_8_out[0]));
  Multiplexer #(.select(3), .width(8)) multiplexer_10 (
    .in0(dipswitch_1_p1), .in1(button_8_out), .out(multiplexer_10_out), .sel(multiplexer_2_out[2:0]));  // open: in2, in3, in4, in5, in6, in7
endmodule
